// Digital circuit t2h.dig as structural Verilog
// The T2H processor is a one clock Harvard 16 bit implementation of a small subset of the Inmos Transputer
module t2h (
  input  reset,
  input  clock,
  input  [7:0] Inst,
  input  [15:0] dIn,
  output [15:0] I,
  output [15:0] Addr,
  output wr,
  output rd,
  output [15:0] dOut
);

  Register #(.Bits(16)) u_I ();  // open: D, C, en, Q
  Register #(.Bits(16)) A ();  // open: D, C, en, Q
  Register #(.Bits(16)) B ();  // open: D, C, en, Q
  Register #(.Bits(16)) C ();  // open: D, C, en, Q
  Register #(.Bits(16)) W ();  // open: D, C, en, Q
  Register #(.Bits(12)) O ();  // open: D, C, en, Q

  assign Addr = 16'h1;
  assign dOut = 16'h1;
  assign I = 16'h1;
  assign rd = 1'b0;
  assign wr = 1'b0;

  // Notes on the sheet:
  //   I: program counter
  //   Addr: Data memory address
  //   wr: write to memory
  //   rd: indicates a read cycle from memory
  //   Inst: instruction to be executed
  //   dIn: data from memory
  //   dOut: data output to memory
endmodule
