// Digital circuit controlUnit.dig as structural Verilog
// generates control signals for datapath
module controlUnit (
  input  clock,
  input  reset,
  input  [15:0] dIn,
  input  alt,
  input  NE,
  input  GE,
  output wr,
  output rd,
  output sign,
  output word,
  output sub,
  output \logic ,
  output [1:0] logSelect,
  output [11:0] topImm,
  output even,
  output const2,
  output selImm,
  output selConst,
  output Azero,
  output we,
  output [3:0] Rw,
  output [3:0] Ra,
  output [3:0] Rb,
  output selRd,
  output slt,
  output immLow
);

  wire and_1_out, and_2_out, and_4_out, and_6_out, and_7_out, and_8_out, and_9_out, and_10_out, and_11_out,
       and_12_out, and_19_out, and_20_out, branch, cond, d_ff_2_q, E, EJ, F, FJorBT, imm, IR2, IR3,
       multiplexer_2_out, or_1_out, or_8_out, prefix_q, xor_1_out, zD, zS1, zS2;
  wire [11:0] multiplexer_1_out;
  wire [15:8] IR_q;

  Multiplexer #(.Bits(12)) multiplexer_1 (
    .sel(d_ff_2_q), .in_0({IR_q, Rb}), .in_1({12{1'b0}}), .out(multiplexer_1_out));
  and and_1 (and_1_out, ~dIn[0], ~dIn[1], ~dIn[2], ~dIn[3], F);  // And
  and and_2 (and_2_out, ~IR3, ~IR2, ~logSelect[1], ~logSelect[0]);  // And
  Multiplexer multiplexer_2 (.sel(logSelect[0]), .in_0(NE), .in_1(GE), .out(multiplexer_2_out));
  xor xor_1 (xor_1_out, multiplexer_2_out, alt);
  D_FF d_ff_1 (.D(reset), .C(clock), .Q(Azero));  // open: nQ
  Register #(.Bits(16)) IR (.D(dIn), .C(clock), .en(F), .Q({IR_q, Rb, IR3, IR2, logSelect}));
  Register #(.Bits(12)) IM (.D(multiplexer_1_out), .C(clock), .en(F), .Q(topImm));
  D_FF fetch (.D(or_1_out), .C(clock), .Q(F), .nQ(E));
  // Probe IR on {IR_q, Rb, IR3, IR2, logSelect}
  or or_1 (or_1_out, E, Azero, and_1_out);
  Register prefix (.D(and_2_out), .C(clock), .en(F), .Q(prefix_q));
  // Probe IM on topImm
  D_FF d_ff_2 (.D(E), .C(clock), .Q(d_ff_2_q));  // open: nQ
  and and_3 (zS2, E, ~Rb[0], ~Rb[1], ~Rb[2], ~Rb[3]);  // And
  or or_2 (imm, prefix_q, ~IR3);  // Or
  and and_4 (and_4_out, ~IR3, ~IR2, ~logSelect[1], logSelect[0]);  // And
  and and_5 (branch, ~IR3, ~IR2, logSelect[1]);  // And
  // Probe fetch on F
  D_FF d_ff_3 (.D(xor_1_out), .C(clock), .Q(cond));  // open: nQ
  and and_6 (and_6_out, E, ~IR2, ~logSelect[1], ~logSelect[0]);  // And
  and and_7 (and_7_out, E, ~IR3, IR2);  // And
  and and_8 (and_8_out, and_4_out, alt);
  or or_3 (selRd, and_6_out, and_7_out);
  and and_9 (and_9_out, F, ~and_8_out);  // And
  and and_10 (and_10_out, F, ~Azero);  // And
  and and_11 (and_11_out, ~EJ, E, imm);  // And
  and and_12 (and_12_out, F, ~FJorBT);  // And
  r0 r0_1 (.rin(IR_q[11:8]), .pc(or_8_out), .rout(Ra), .z(zS1));
  and and_13 (wr, E, ~IR3, IR2, logSelect[1]);  // And
  or or_4 (rd, F, ~logSelect[1]);  // Or
  and and_14 (sub, E, ~IR2, logSelect[1]);  // And
  and and_15 (\logic , E, IR3, IR2);
  nand nand_1 (we, E, branch);
  r0 r0_2 (.rin(IR_q[15:12]), .pc(F), .rout(Rw), .z(zD));
  and and_16 (slt, E, ~IR2, logSelect[1], logSelect[0]);  // And
  and and_17 (immLow, F, ~IR3, logSelect[1]);  // And
  and and_18 (EJ, E, and_4_out);
  and and_19 (and_19_out, F, and_4_out);
  and and_20 (and_20_out, F, branch, cond);
  or or_5 (const2, and_10_out, EJ);
  or or_6 (selImm, FJorBT, and_11_out);
  or or_7 (selConst, EJ, and_12_out, zS2);
  or or_8 (or_8_out, and_9_out, EJ);
  or or_9 (FJorBT, and_19_out, and_20_out);
  not not_1 (sign, IR3);

  assign even = const2;
  assign word = logSelect[0];

  // Other names for the same wires on the sheet: IR0 = logSelect[0]; IR1 = logSelect[1]

  // Notes on the sheet:
  //   clock: controls internal registers
  //   reset: when high forces the PC to 0x0000
  //   dIn: data from memory
  //   alt: immediate value indicates alternative instruction in lowest bit
  //   NE: A ~= B
  //   GE: A >= B
  //   wr: memory write cycle
  //   rd: memory read cycle
  //   sign: not LBU
  //   word: not SB, LB or LBU
  //   sub: change addition to subtraction
  //   logic: select logic operation instead of addition
  //   logSelect: selects between shift right, AND, OR, XOR
  //   topImm: saved from prefix instruction
  //   even: forces bottom bit of immediate to 0
  //   const2: changes constant from 0 to 2
  //   selImm: B is immediate
  //   selConst: B is a constant
  //   Azero: force A to 0
  //   we: updates register Rw
  //   Rw: register to be written
  //   Ra: first register to read
  //   Rb: second register to read
  //   selRd: selects betweenALU result and memory for write back
  //   slt: ignores ALU result and use GE?0x0000:0x0001
  //   immLow: selects either field rS2 or rD for the 4 lower bits of immediate
endmodule
