// Digital circuit drv16.dig as structural Verilog
// 16 bit processor which is compatible at the assembly language level with RISC-V
module drv16 (
  input  clock,
  input  reset,
  input  [15:0] dIn,
  output [14:0] addr,
  output wr,
  output [15:0] dOut,
  output rd
);

  wire sign, undriven_3, word;
  wire [15:0] multiplexer_4_out, rD_t, rS2;
  wire [15:7] and_1_out;
  wire [15:8] multiplexer_1_out, multiplexer_2_out, multiplexer_3_out, multiplexer_5_out, undriven,
       undriven_2, undriven_4, undriven_5;

  and and_1 (and_1_out[7], rD_t[7], sign);
  Multiplexer #(.Bits(16)) multiplexer_1 (
    .sel(undriven_3), .in_0({undriven_2, dIn[7:0]}), .in_1({undriven, dIn[15:8]}),
    .out({multiplexer_1_out, rD_t[7:0]}));
  Multiplexer #(.Bits(16)) multiplexer_2 (
    .sel(word), .in_0({and_1_out, {7{and_1_out[7]}}}), .in_1({undriven, dIn[15:8]}),
    .out({multiplexer_2_out, rD_t[15:8]}));
  Multiplexer #(.Bits(16)) multiplexer_3 (
    .sel(undriven_3), .in_0({undriven_5, rS2[7:0]}), .in_1({undriven_2, dIn[7:0]}),
    .out({multiplexer_3_out, dOut[7:0]}));
  Multiplexer #(.Bits(16)) multiplexer_4 (
    .sel(undriven_3), .in_0({undriven, dIn[15:8]}), .in_1({undriven_5, rS2[7:0]}), .out(multiplexer_4_out));
  Multiplexer #(.Bits(16)) multiplexer_5 (
    .sel(word), .in_0(multiplexer_4_out), .in_1({undriven_4, rS2[15:8]}),
    .out({multiplexer_5_out, dOut[15:8]}));
  // Pins of 8 and 16 bits meet at {undriven_5, rS2[7:0]}
  // Pins of 8 and 16 bits meet at {undriven_2, dIn[7:0]}
  // Pins of 8 and 16 bits meet at {multiplexer_3_out, dOut[7:0]}
  // Pins of 8 and 16 bits meet at {undriven_4, rS2[15:8]}
  // Pins of 8 and 16 bits meet at {multiplexer_5_out, dOut[15:8]}
  // Pins of 8 and 16 bits meet at {undriven, dIn[15:8]}
  // Pins of 8 and 16 bits meet at {multiplexer_1_out, rD_t[7:0]}
  // Pins of 8 and 16 bits meet at {and_1_out, {7{and_1_out[7]}}}
  // Pins of 8 and 16 bits meet at {multiplexer_2_out, rD_t[15:8]}

  assign rd = 1'b1;
  assign wr = reset;

  // Notes on the sheet:
  //   addr: selects a 16 bit word in memory to be read or changed
  //   wr: indicates a write operation
  //   dOut: word to be sent to memory
  //   reset: when high prepares the processor to execute from address 0
  //   dIn: word coming from memory
  //   rd: indicates that memory will be read in this cycle
endmodule
