// Digital circuit system.dig as structural Verilog
// A simple system with a drv16 processor, 64KB of RAM, a terminal and keyboard
module system (
  input  clk,
  output [31:0] cnt
);

  wire cpu_p6, cpu_p7, cpu_p8, reset_out;
  wire [14:0] cpu_p4;
  wire [15:0] cpu_p3, cpu_p5, mem0_low_d;

  DipSwitch reset (.out(reset_out));
  // Probe dIn on cpu_p3
  // drv16 cpu: pin names not known; wires that end beside it: clk, reset_out, cpu_p3, cpu_p4, cpu_p5, cpu_p6, cpu_p7, cpu_p8
  // Probe addr on cpu_p4
  RAMDualPort #(.AddrBits(15), .isProgramMemory("true"), .Bits(8)) mem0_low (
    .A(cpu_p4), .Din(cpu_p5[7:0]), .str(cpu_p8), .C(clk), .ld(cpu_p6), .D(mem0_low_d[7:0]));
  RAMDualPort #(.AddrBits(15), .isProgramMemory("true"), .Bits(8)) mem1_high (
    .A(cpu_p4), .Din(cpu_p5[15:8]), .str(cpu_p7), .C(clk), .ld(cpu_p6), .D(mem0_low_d[15:8]));
  termcnt termcnt_1 (
    .relogio(clk), .write(cpu_p8), .read(cpu_p6), .Addr({{17{1'b1}}, cpu_p4}), .dMemOut(mem0_low_d),
    .dIn(cpu_p5), .dOut(cpu_p3), .cnt(cnt));

  // Notes on the sheet:
  //   clk: Hz: 2147483647
  //   cnt: number of clocks for benchmark
endmodule
